# Fritzing sketch HumidifierController (saved by Fritzing 0.9.2b)
circuit board: 4.23427cm x 5.57953cm
breadboards: 1

parts:
  Part2 = Arduino Nano (Rev3.0)
  Q1 = NPN-Transistor [package="TO92 [THT]"]
  R1 = Resistor [tolerance=±5% resistance=22k package="0805 [SMD]"]
  R2 = Resistor [tolerance=±5% resistance=680 package="0805 [SMD]"]
  R3 = Resistor [tolerance=±5% resistance=220 package="0805 [SMD]"]
  C1 = Electrolytic Capacitor [capacitance=47µF voltage=50V package="0405 [SMD, electrolytic]"]
  D2 = Diode [package=diode-1n4001]
  D3 = Zener Diode [part_number=1N5249B package="300 mil [THT]"]
  F1 = FUSE [package=fuse_5mm]
  JP1 = Header 3 [package=screwterminal-3.5mm-3_lock.007s]
  D1 = Diode [package=diode-1n4001]

nets:
  N1: Part2.GND, R2.Pin_0, R2.Pin_1, C1.-, D2.A, D3.anode, JP1.2
  N2: Part2.D2, R1.Pin_0
  N3: Part2.VIN, C1.+, D3.cathode, F1.1
  N4: Q1.E, R3.Pin_1
  N5: Q1.B, R1.Pin_1
  N6: R3.Pin_0, D2.C, JP1.1
  N7: F1.2, D1.C
  N8: JP1.3, D1.A

custom parts:
  Zener Diode: A standard zener diode
